# Fritzing sketch Diagrama (saved by Fritzing 0.9.6b)

parts:
  Mod1 = KY-019 5V Relay Module [package="Breakout board"]
  U1 = ESP32-38PinWide [part_number=ESP32-38PinWide]
  LED1 = smd LED [color="Red (633nm)" package="0805 [SMD]"]
  U2 = BATTERY-2 [package=battery-aa]
  BAT1 = BC9VPC [package=bc9vpc]

nets:
  N1: Mod1.S, U1.GPIO12
  N2: Mod1.+, U1.VIN, BAT1.V+
  N3: Mod1.-, U1.GND, U1.GPIO13, BAT1.V-
  N4: Mod1.Common, LED1.anode
  N5: Mod1.NO, U2.+1
  N6: LED1.cathode, U2.-1

custom parts:
  KY-019 5V Relay Module: KY-019 5V Relay module, used to control AC circuits. (Special thanks to vanepp for fixing the PCB holes and other errors)
  ESP32-38PinWide: Generic 38-Pin ESP32 with wide format (only access to one side of pins on a breadboard) based on Stephen Lilley's HiLetgo ESP-WROOM-32 ESP32 ESP-32S Development Board.
